// Logisim project CPU.circ as structural Verilog: 13 circuits, main circuit main
module main (
  output NOP,
  output [6:0] out_2
);

  wire _1, _2, _3, CLEAR, CLK, G_C, G_E, G_P, G_W_R, keyboard_1_avail, PRNT;
  wire [2:0] G_P_A;
  wire [3:0] Adress_out_2, Adress_out_3, Adress_out_4, Adress_out_5, G_A, n8_to_4_de_verdad_1_out_2,
       n8_to_4_de_verdad_1_out_3, n8_to_4_de_verdad_2_out_2, n8_to_4_de_verdad_2_out_3,
       n8_to_4_de_verdad_3_out_2, n8_to_4_de_verdad_3_out_3, n8_to_4_de_verdad_4_out_2,
       n8_to_4_de_verdad_4_out_3, n8_to_4_de_verdad_5_out_2, n8_to_4_de_verdad_5_out_3;
  wire [6:0] K_Y;
  wire [7:0] r0, r1, r2, r3, R_A;
  wire [11:0] G_D, gpu_1_out_9, gpu_1_out_10, gpu_1_out_11, gpu_1_out_12, gpu_1_out_13, gpu_1_out_14,
       gpu_1_out_15, gpu_1_out_16;
  wire [15:0] cpu_1_adress;
  wire [19:0] rom_1_data;

  Hex_Digit_Display hex_digit_display_1 (.value(Adress_out_3));  // open: dp
  Hex_Digit_Display hex_digit_display_2 (.value(Adress_out_2));  // open: dp
  ROM rom_1 (.Adress(cpu_1_adress), .Data(rom_1_data));
  Hex_Digit_Display hex_digit_display_3 (.value(n8_to_4_de_verdad_1_out_3));  // open: dp
  Hex_Digit_Display hex_digit_display_4 (.value(n8_to_4_de_verdad_1_out_2));  // open: dp
  _8_to_4_de_verdad u_8_to_4_de_verdad_1 (
    .out_2(n8_to_4_de_verdad_1_out_2), .out_3(n8_to_4_de_verdad_1_out_3), .in_1(r0));
  Hex_Digit_Display hex_digit_display_5 (.value(Adress_out_4));  // open: dp
  Clock clock_1 (.out(CLK));
  Hex_Digit_Display hex_digit_display_6 (.value(Adress_out_5));  // open: dp
  _8_to_4 Adress (
    .out_3(Adress_out_3), .out_4(Adress_out_4), .in_1(cpu_1_adress), .out_5(Adress_out_5),
    .out_2(Adress_out_2));
  Hex_Digit_Display hex_digit_display_7 (.value(n8_to_4_de_verdad_2_out_2));  // open: dp
  Hex_Digit_Display hex_digit_display_8 (.value(n8_to_4_de_verdad_2_out_3));  // open: dp
  _8_to_4_de_verdad u_8_to_4_de_verdad_2 (
    .out_2(n8_to_4_de_verdad_2_out_2), .out_3(n8_to_4_de_verdad_2_out_3), .in_1(r1));
  CPU cpu_1 (
    .NADA(NOP), .Adress(cpu_1_adress), .CLK(CLK), .r0(r0), .r1(r1), .r2(r2), .r4(r3), .in_1(rom_1_data),
    .PRNT(PRNT), .CLEAR(CLEAR), .Ram_Adress(R_A), .data_print(out_2), .Input_1(_1), .Input_2(_2),
    .Keyboard(K_Y), .Escribir_GPU(G_E), .Data_to_WRT(G_D), .Adress_to_WRT(G_A), .Gpu_Clear(G_C),
    .Input_3(_3), .E_P_G(G_P), .E_P_G_A(G_P_A), .G_P_R(G_W_R));  // open: in_7, in_8
  Hex_Digit_Display hex_digit_display_9 (.value(n8_to_4_de_verdad_3_out_2));  // open: dp
  Hex_Digit_Display hex_digit_display_10 (.value(n8_to_4_de_verdad_3_out_3));  // open: dp
  _8_to_4_de_verdad u_8_to_4_de_verdad_3 (
    .out_2(n8_to_4_de_verdad_3_out_2), .out_3(n8_to_4_de_verdad_3_out_3), .in_1(r2));
  TTY tty_1 (.data(out_2), .clk(CLK), .we(PRNT), .clr(CLEAR));
  Hex_Digit_Display hex_digit_display_11 (.value(n8_to_4_de_verdad_4_out_2));  // open: dp
  Hex_Digit_Display hex_digit_display_12 (.value(n8_to_4_de_verdad_4_out_3));  // open: dp
  _8_to_4_de_verdad u_8_to_4_de_verdad_4 (
    .out_2(n8_to_4_de_verdad_4_out_2), .out_3(n8_to_4_de_verdad_4_out_3), .in_1(r3));
  Keyboard keyboard_1 (.clk(CLK), .re(keyboard_1_avail), .avail(keyboard_1_avail), .data(K_Y));  // open: clr
  Hex_Digit_Display hex_digit_display_13 (.value(n8_to_4_de_verdad_5_out_2));  // open: dp
  DotMatrix #(.inputtype("row"), .matrixcols(12), .matrixrows(8)) dotmatrix_1 (
    .row0(gpu_1_out_9), .row1(gpu_1_out_10), .row2(gpu_1_out_11), .row3(gpu_1_out_12), .row4(gpu_1_out_13),
    .row5(gpu_1_out_14), .row6(gpu_1_out_15), .row7(gpu_1_out_16));
  GPU gpu_1 (
    .Dta_to_Wrt(G_D), .Clear(G_C), .Adress_to_WRT(G_A), .CLK(CLK), .Escribiendo(G_E), .out_9(gpu_1_out_9),
    .out_10(gpu_1_out_10), .out_11(gpu_1_out_11), .out_12(gpu_1_out_12), .out_13(gpu_1_out_13),
    .out_14(gpu_1_out_14), .out_15(gpu_1_out_15), .out_16(gpu_1_out_16), .Escribir_Predt(G_P),
    .Predt_A(G_P_A), .G_W_R(G_W_R));
  Hex_Digit_Display hex_digit_display_14 (.value(n8_to_4_de_verdad_5_out_3));  // open: dp
  _8_to_4_de_verdad u_8_to_4_de_verdad_5 (
    .out_2(n8_to_4_de_verdad_5_out_2), .out_3(n8_to_4_de_verdad_5_out_3), .in_1(R_A));
  Button button_1 (.out(_1));
  Button button_2 (.out(_2));
  Button button_3 (.out(_3));

  // Notes on the sheet:
  //   r0
  //   r1
  //   r2
  //   r3
  //   Ram Adress
endmodule

module ALU (
  input  [7:0] A,
  input  [7:0] B,
  input  ADD,
  input  SUB,
  input  ADDI,
  output [7:0] Result
);

  wire nor_1_out;
  wire [7:0] adder_1_out, adder_2_out, subtractor_1_out;

  Adder adder_1 (.a(A), .b(B), .out(adder_1_out));  // open: cin, cout
  Subtractor subtractor_1 (.a(A), .b(B), .out(subtractor_1_out));  // open: bin, bout
  Adder adder_2 (.a(A), .b(B), .out(adder_2_out));  // open: cin, cout
  nor nor_1 (nor_1_out, ADD, ADDI, SUB);
  assign Result = ADD ? adder_1_out : 8'bz;  // Controlled_Buffer controlled_buffer_1
  assign Result = SUB ? subtractor_1_out : 8'bz;  // Controlled_Buffer controlled_buffer_2
  assign Result = ADDI ? adder_2_out : 8'bz;  // Controlled_Buffer controlled_buffer_3
  assign Result = nor_1_out ? {8{1'b0}} : 8'bz;  // Controlled_Buffer controlled_buffer_4
endmodule

module CPU (
  input  [19:0] in_1,
  input  Input_1,
  input  Input_2,
  input  Input_3,
  input  CLK,
  input  [6:0] Keyboard,
  input  in_7,
  input  in_8,
  output NADA,
  output Gpu_Clear,
  output CLEAR,
  output PRNT,
  output G_P_R,
  output [15:0] Adress,
  output [7:0] r0,
  output [7:0] r1,
  output [7:0] Ram_Adress,
  output [7:0] r2,
  output [7:0] r4,
  output Escribir_GPU,
  output [11:0] Data_to_WRT,
  output [6:0] data_print,
  output [3:0] Adress_to_WRT,
  output E_P_G,
  output [2:0] E_P_G_A
);

  wire and_1_out, and_2_out, comparator_1_eq, controlled_buffer_8_out, decoder_1_out0, decoder_1_out1,
       decoder_1_out2, decoder_1_out3, demultiplexer_1_out0, demultiplexer_1_out1, demultiplexer_1_out2,
       demultiplexer_1_out3, demultiplexer_2_out1, not_1_out, not_2_out, not_3_out, not_4_out, not_5_out,
       not_6_out, op_decoder_1_add, op_decoder_1_addi, op_decoder_1_addm, op_decoder_1_alu_op,
       op_decoder_1_data_in_r, op_decoder_1_if, op_decoder_1_jmp, op_decoder_1_prnt, op_decoder_1_prnt_k,
       op_decoder_1_r_r, op_decoder_1_sub, or_1_out;
  wire [6:0] shift_register_1_q0, shift_register_1_q1, shift_register_1_q2;
  wire [7:0] alu_1_result, controlled_buffer_6_out_2, memoria_1_out_7, multiplexer_3_out, multiplexer_4_out,
       multiplexer_5_out, multiplexer_6_out, multiplexer_7_out, multiplexer_8_out, multiplexer_9_out,
       multiplexer_10_out;
  wire [7:7] controlled_buffer_5_out;
  wire [15:0] adder_1_out, multiplexer_1_out, multiplexer_2_out;
  wire [19:0] controlled_buffer_6_out;

  and and_1 (and_1_out, ~op_decoder_1_jmp, ~controlled_buffer_8_out);  // AND_Gate
  Multiplexer #(.width(16), .enable("false")) multiplexer_1 (
    .in0(in_1[15:0]), .in1({{7{1'b0}}, in_1[8:0]}), .out(multiplexer_1_out), .sel(controlled_buffer_8_out));
  Multiplexer #(.width(16), .enable("false")) multiplexer_2 (
    .in0(multiplexer_1_out), .in1(adder_1_out), .out(multiplexer_2_out), .sel(and_1_out));
  Register #(.width(16)) register_1 (.D(multiplexer_2_out), .Q(Adress), .clk(CLK));  // open: en, clr
  or or_1 (or_1_out, op_decoder_1_addm, op_decoder_1_prnt);
  not not_1 (not_1_out, op_decoder_1_addm);
  Shift_Register #(.width(7), .length(3)) shift_register_1 (
    .in(Keyboard), .clk(CLK), .q0(shift_register_1_q0), .q1(shift_register_1_q1), .q2(shift_register_1_q2));  // open: shift, out, load, clr, d0, d1, d2
  and and_2 (and_2_out, ~in_7, ~in_8);  // AND_Gate
  OP_Decoder op_decoder_1 (
    .in_1(in_1[19:16]), .NOP(NADA), .ADD(op_decoder_1_add), .SUB(op_decoder_1_sub), .JMP(op_decoder_1_jmp),
    .R_R(op_decoder_1_r_r), .ADDI(op_decoder_1_addi), .PRNT(op_decoder_1_prnt), .CLEAR(CLEAR),
    .ADDM(op_decoder_1_addm), .IF(op_decoder_1_if), .PRNT_K(op_decoder_1_prnt_k), .GPU(Escribir_GPU),
    .GPU_Clear(Gpu_Clear), .out_15(E_P_G), .out_16(G_P_R), .ALU_OP(op_decoder_1_alu_op),
    .DATA_IN_R(op_decoder_1_data_in_r));  // open: out_17
  not not_2 (not_2_out, or_1_out);
  assign PRNT = not_3_out ? op_decoder_1_prnt : 1'bz;  // Controlled_Buffer controlled_buffer_1
  not not_3 (not_3_out, op_decoder_1_prnt_k);
  Adder #(.width(16)) adder_1 (.a(Adress), .b(16'h1), .out(adder_1_out));  // open: cin, cout
  memoria memoria_1 (
    .Adress(controlled_buffer_6_out[7:0]), .CLK(CLK), .L_E(not_1_out), .L(op_decoder_1_prnt),
    .E(op_decoder_1_addm), .out_7(memoria_1_out_7), .in_3(controlled_buffer_6_out_2));
  assign Ram_Adress = not_2_out ? {8{1'b0}} : 8'bz;  // Controlled_Buffer controlled_buffer_2
  not not_4 (not_4_out, op_decoder_1_prnt_k);
  assign PRNT = op_decoder_1_prnt_k ? op_decoder_1_prnt_k : 1'bz;  // Controlled_Buffer controlled_buffer_3
  assign Ram_Adress = or_1_out ? controlled_buffer_6_out_2 : 8'bz;  // Controlled_Buffer controlled_buffer_4
  assign {controlled_buffer_5_out[7], data_print} = not_4_out ? memoria_1_out_7 : 8'bz;  // Controlled_Buffer controlled_buffer_5
  assign {controlled_buffer_6_out[19:16], controlled_buffer_6_out_2, controlled_buffer_6_out[7:0]} = or_1_out ? in_1 : 20'bz;  // Controlled_Buffer controlled_buffer_6
  assign {controlled_buffer_5_out[7], data_print} = op_decoder_1_prnt_k ? {1'b0, shift_register_1_q1} : 8'bz;  // Controlled_Buffer controlled_buffer_7
  ALU alu_1 (
    .A(multiplexer_4_out), .B(multiplexer_5_out), .ADD(op_decoder_1_add), .SUB(op_decoder_1_sub),
    .ADDI(op_decoder_1_addi), .Result(alu_1_result));
  Multiplexer #(.width(8), .enable("false")) multiplexer_3 (
    .in1(alu_1_result), .out(multiplexer_3_out), .sel(op_decoder_1_data_in_r));  // open: in0
  Decoder #(.select(2), .enable("false")) decoder_1 (
    .out0(decoder_1_out0), .out1(decoder_1_out1), .out2(decoder_1_out2), .out3(decoder_1_out3),
    .sel(in_1[9:8]));
  Demultiplexer #(.select(2), .enable("false")) demultiplexer_1 (
    .out0(demultiplexer_1_out0), .out1(demultiplexer_1_out1), .out2(demultiplexer_1_out2),
    .out3(demultiplexer_1_out3), .in(op_decoder_1_r_r), .sel(in_1[9:8]));
  Multiplexer #(.width(8), .enable("false")) multiplexer_4 (
    .in1(multiplexer_6_out), .out(multiplexer_4_out), .sel(op_decoder_1_alu_op));  // open: in0
  Multiplexer #(.width(8), .enable("false")) multiplexer_5 (
    .in0(in_1[7:0]), .in1(multiplexer_8_out), .out(multiplexer_5_out), .sel(demultiplexer_2_out1));
  Demultiplexer #(.enable("false")) demultiplexer_2 (
    .out1(demultiplexer_2_out1), .in(op_decoder_1_alu_op), .sel(not_5_out));  // open: out0
  not not_5 (not_5_out, op_decoder_1_addi);
  Comparator comparator_1 (.a(multiplexer_9_out), .b(multiplexer_10_out), .eq(comparator_1_eq));  // open: gt, lt
  assign controlled_buffer_8_out = op_decoder_1_if ? comparator_1_eq : 1'bz;  // Controlled_Buffer controlled_buffer_8
  not not_6 (not_6_out, op_decoder_1_if);
  Multiplexer #(.select(2), .width(8), .enable("false")) multiplexer_6 (
    .in0(r0), .in1(r1), .in2(r2), .in3(r4), .out(multiplexer_6_out), .sel(in_1[9:8]));
  Register register_2 (.D(multiplexer_3_out), .en(decoder_1_out0), .Q(r0), .clk(CLK), .clr(demultiplexer_1_out0));
  Register register_3 (.D(multiplexer_3_out), .en(decoder_1_out1), .Q(r1), .clk(CLK), .clr(demultiplexer_1_out1));
  Register register_4 (.D(multiplexer_3_out), .en(decoder_1_out2), .Q(r2), .clk(CLK), .clr(demultiplexer_1_out2));
  Register register_5 (.D(multiplexer_3_out), .en(decoder_1_out3), .Q(r4), .clk(CLK), .clr(demultiplexer_1_out3));
  Multiplexer #(.select(2), .width(8), .enable("false")) multiplexer_7 (
    .in0(r0), .in1(r1), .in2(r2), .in3(r4), .out(multiplexer_7_out), .sel(in_1[15:14]));
  assign controlled_buffer_8_out = not_6_out ? 1'b0 : 1'bz;  // Controlled_Buffer controlled_buffer_9
  Multiplexer #(.select(2), .width(8), .enable("false")) multiplexer_8 (
    .in0(r0), .in1(r1), .in2(r2), .in3(r4), .out(multiplexer_8_out), .sel(in_1[1:0]));
  assign E_P_G_A = G_P_R ? multiplexer_7_out[2:0] : 3'bz;  // Controlled_Buffer controlled_buffer_10
  assign Data_to_WRT = Escribir_GPU ? in_1[11:0] : 12'bz;  // Controlled_Buffer controlled_buffer_11
  assign E_P_G_A = E_P_G ? in_1[15:13] : 3'bz;  // Controlled_Buffer controlled_buffer_12
  Multiplexer #(.select(3), .width(8), .enable("false")) multiplexer_9 (
    .in0(r0), .in1(r1), .in2(r2), .in3(r4), .in4({8{1'b0}}), .in5(8'h1), .in6(8'h3b),
    .out(multiplexer_9_out), .sel(in_1[15:13]));  // open: in7
  Multiplexer #(.select(4), .width(8), .enable("false")) multiplexer_10 (
    .in0(r0), .in1(r1), .in2(r2), .in3(r4), .in4({{7{1'b0}}, Input_1}), .in5({{7{1'b0}}, Input_2}),
    .in6({1'b0, shift_register_1_q2}), .in7({1'b0, shift_register_1_q0}), .in8({{7{1'b0}}, Input_3}),
    .out(multiplexer_10_out), .sel(in_1[12:9]));  // open: in9, in10, in11, in12, in13, in14, in15

  assign Adress_to_WRT = in_1[15:12];
endmodule

module OP_Decoder (
  input  [3:0] in_1,
  output NOP,
  output ADD,
  output SUB,
  output JMP,
  output R_R,
  output ADDI,
  output PRNT,
  output CLEAR,
  output ADDM,
  output IF,
  output PRNT_K,
  output GPU,
  output GPU_Clear,
  output out_15,
  output out_16,
  output out_17,
  output ALU_OP,
  output DATA_IN_R
);

  or or_1 (ALU_OP, ADD, ADDI, SUB);
  or or_2 (DATA_IN_R, ADD, ADDI, SUB);
  and and_1 (NOP, ~in_1[0], ~in_1[1], ~in_1[2], ~in_1[3]);  // AND_Gate
  and and_2 (ADD, in_1[0], ~in_1[1], ~in_1[2], ~in_1[3]);  // AND_Gate
  and and_3 (SUB, ~in_1[0], in_1[1], ~in_1[2], ~in_1[3]);  // AND_Gate
  and and_4 (JMP, in_1[0], in_1[1], ~in_1[2], ~in_1[3]);  // AND_Gate
  and and_5 (R_R, ~in_1[0], ~in_1[1], in_1[2], ~in_1[3]);  // AND_Gate
  and and_6 (ADDI, in_1[0], ~in_1[1], in_1[2], ~in_1[3]);  // AND_Gate
  and and_7 (PRNT, ~in_1[0], in_1[1], in_1[2], ~in_1[3]);  // AND_Gate
  and and_8 (CLEAR, in_1[0], in_1[1], in_1[2], ~in_1[3]);  // AND_Gate
  and and_9 (ADDM, ~in_1[0], ~in_1[1], ~in_1[2], in_1[3]);  // AND_Gate
  and and_10 (IF, in_1[0], ~in_1[1], ~in_1[2], in_1[3]);  // AND_Gate
  and and_11 (PRNT_K, ~in_1[0], in_1[1], ~in_1[2], in_1[3]);  // AND_Gate
  and and_12 (GPU, in_1[0], in_1[1], ~in_1[2], in_1[3]);  // AND_Gate
  and and_13 (GPU_Clear, ~in_1[0], ~in_1[1], in_1[2], in_1[3]);  // AND_Gate
  and and_14 (out_15, in_1[0], ~in_1[1], in_1[2], in_1[3]);  // AND_Gate
  and and_15 (out_16, ~in_1[0], in_1[1], in_1[2], in_1[3]);  // AND_Gate
  and and_16 (out_17, in_1[0], in_1[1], in_1[2], in_1[3]);
endmodule

module _8_to_4 (
  input  [15:0] in_1,
  output [3:0] out_2,
  output [3:0] out_3,
  output [3:0] out_4,
  output [3:0] out_5
);


  assign out_2 = in_1[15:12];
  assign out_3 = in_1[11:8];
  assign out_4 = in_1[7:4];
  assign out_5 = in_1[3:0];
endmodule

module ROM (
  input  [15:0] Adress,
  output [19:0] Data
);

  ROM_part #(.addrWidth(16), .dataWidth(20)) rom_1 (.addr(Adress), .data(Data));  // open: sel

  // Notes on the sheet:
  //   contents of rom_1 (hex, n*v repeats v):
  //   d4000 30020 14*0 50002 50101 20001 e0000 30014 331*0 da000 447*0 d2000 351*0 dc000 447*0 30010
endmodule

module _8_to_4_de_verdad (
  input  [7:0] in_1,
  output [3:0] out_2,
  output [3:0] out_3
);


  assign out_2 = in_1[7:4];
  assign out_3 = in_1[3:0];
endmodule

module Memory (
  input  [7:0] in_1,
  input  [7:0] ADRESS,
  input  CLK,
  input  L_E,
  input  Escritura,
  input  Lectura,
  output [7:0] OUT
);

  wire controlled_buffer_1_out, or_1_out;

  assign controlled_buffer_1_out = or_1_out ? CLK : 1'bz;  // Controlled_Buffer controlled_buffer_1
  or or_1 (or_1_out, Escritura, Lectura);
  RAM ram_1 (.addr(ADRESS), .data(OUT), .clk(controlled_buffer_1_out), .ld(L_E));  // open: sel, clr
  assign OUT = Escritura ? in_1 : 8'bz;  // Controlled_Buffer controlled_buffer_2
endmodule

module memoria (
  input  [7:0] Adress,
  input  CLK,
  input  [7:0] in_3,
  input  L_E,
  input  L,
  input  E,
  output [7:0] out_7
);

  wire controlled_buffer_1_out, or_1_out;

  assign controlled_buffer_1_out = or_1_out ? CLK : 1'bz;  // Controlled_Buffer controlled_buffer_1
  or or_1 (or_1_out, L, E);
  RAM ram_1 (.addr(Adress), .data(out_7), .clk(controlled_buffer_1_out), .ld(L_E));  // open: sel, clr
  assign out_7 = E ? in_3 : 8'bz;  // Controlled_Buffer controlled_buffer_2
endmodule

module GPU (
  input  [11:0] Dta_to_Wrt,
  input  Clear,
  input  [3:0] Adress_to_WRT,
  input  CLK,
  input  Escribiendo,
  input  Escribir_Predt,
  input  [2:0] Predt_A,
  input  G_W_R,
  output [11:0] out_9,
  output [11:0] out_10,
  output [11:0] out_11,
  output [11:0] out_12,
  output [11:0] out_13,
  output [11:0] out_14,
  output [11:0] out_15,
  output [11:0] out_16
);

  wire controlled_buffer_1_out, controlled_buffer_2_out, decoder_1_out0, decoder_1_out1, decoder_1_out2,
       decoder_1_out3, decoder_1_out4, decoder_1_out5, decoder_1_out6, decoder_1_out7, demultiplexer_1_out0,
       demultiplexer_1_out1, demultiplexer_1_out2, demultiplexer_1_out3, demultiplexer_1_out4,
       demultiplexer_1_out5, demultiplexer_1_out6, demultiplexer_1_out7, not_1_out, or_1_out;
  wire [11:0] controlled_buffer_4_out, controlled_buffer_5_out, controlled_buffer_6_out,
       controlled_buffer_7_out, controlled_buffer_8_out, controlled_buffer_9_out, controlled_buffer_10_out,
       controlled_buffer_11_out;

  assign controlled_buffer_1_out = Escribir_Predt ? Escribir_Predt : 1'bz;  // Controlled_Buffer controlled_buffer_1
  not not_1 (not_1_out, Escribir_Predt);
  assign controlled_buffer_2_out = or_1_out ? CLK : 1'bz;  // Controlled_Buffer controlled_buffer_2
  assign controlled_buffer_1_out = not_1_out ? G_W_R : 1'bz;  // Controlled_Buffer controlled_buffer_3
  or or_1 (or_1_out, Escribir_Predt, G_W_R, Escribiendo);
  Demultiplexer #(.select(3), .enable("false")) demultiplexer_1 (
    .out0(demultiplexer_1_out0), .out1(demultiplexer_1_out1), .out2(demultiplexer_1_out2),
    .out3(demultiplexer_1_out3), .out4(demultiplexer_1_out4), .out5(demultiplexer_1_out5),
    .out6(demultiplexer_1_out6), .out7(demultiplexer_1_out7), .in(controlled_buffer_1_out), .sel(Predt_A));
  assign controlled_buffer_4_out = Escribiendo ? Dta_to_Wrt : 12'bz;  // Controlled_Buffer controlled_buffer_4
  assign controlled_buffer_5_out = Escribiendo ? Dta_to_Wrt : 12'bz;  // Controlled_Buffer controlled_buffer_5
  assign controlled_buffer_6_out = Escribiendo ? Dta_to_Wrt : 12'bz;  // Controlled_Buffer controlled_buffer_6
  assign controlled_buffer_7_out = Escribiendo ? Dta_to_Wrt : 12'bz;  // Controlled_Buffer controlled_buffer_7
  assign controlled_buffer_8_out = Escribiendo ? Dta_to_Wrt : 12'bz;  // Controlled_Buffer controlled_buffer_8
  assign controlled_buffer_9_out = Escribiendo ? Dta_to_Wrt : 12'bz;  // Controlled_Buffer controlled_buffer_9
  assign controlled_buffer_10_out = Escribiendo ? Dta_to_Wrt : 12'bz;  // Controlled_Buffer controlled_buffer_10
  assign controlled_buffer_11_out = Escribiendo ? Dta_to_Wrt : 12'bz;  // Controlled_Buffer controlled_buffer_11
  Decoder #(.select(4)) decoder_1 (
    .out0(decoder_1_out0), .out1(decoder_1_out1), .out2(decoder_1_out2), .out3(decoder_1_out3),
    .out4(decoder_1_out4), .out5(decoder_1_out5), .out6(decoder_1_out6), .out7(decoder_1_out7),
    .sel(Adress_to_WRT), .en(Escribiendo));  // open: out8, out9, out10, out11, out12, out13, out14, out15
  Register #(.width(12)) register_1 (
    .D(controlled_buffer_4_out), .en(decoder_1_out0), .Q(out_9), .clk(controlled_buffer_2_out), .clr(Clear));
  Register #(.width(12)) register_2 (
    .D(controlled_buffer_5_out), .en(decoder_1_out1), .Q(out_10), .clk(controlled_buffer_2_out), .clr(Clear));
  Register #(.width(12)) register_3 (
    .D(controlled_buffer_6_out), .en(decoder_1_out2), .Q(out_11), .clk(controlled_buffer_2_out), .clr(Clear));
  Register #(.width(12)) register_4 (
    .D(controlled_buffer_7_out), .en(decoder_1_out3), .Q(out_12), .clk(controlled_buffer_2_out), .clr(Clear));
  Register #(.width(12)) register_5 (
    .D(controlled_buffer_8_out), .en(decoder_1_out4), .Q(out_13), .clk(controlled_buffer_2_out), .clr(Clear));
  Register #(.width(12)) register_6 (
    .D(controlled_buffer_9_out), .en(decoder_1_out5), .Q(out_14), .clk(controlled_buffer_2_out), .clr(Clear));
  Register #(.width(12)) register_7 (
    .D(controlled_buffer_10_out), .en(decoder_1_out6), .Q(out_15), .clk(controlled_buffer_2_out), .clr(Clear));
  Register #(.width(12)) register_8 (
    .D(controlled_buffer_11_out), .en(decoder_1_out7), .Q(out_16), .clk(controlled_buffer_2_out), .clr(Clear));
  Constante constante_1 (
    ._1_2(controlled_buffer_4_out), ._2_2(controlled_buffer_5_out), ._3_2(controlled_buffer_6_out),
    ._4_2(controlled_buffer_7_out), ._5_2(controlled_buffer_8_out), ._6_2(controlled_buffer_9_out),
    ._7_2(controlled_buffer_10_out), ._8(controlled_buffer_11_out), .Activated(demultiplexer_1_out1),
    ._0(12'h60), ._1(12'h1e0), ._2(12'h60), ._3(12'h60), ._4(12'h60), ._5(12'h60), ._6(12'h60), ._7(12'h1f8));
  Constante constante_2 (
    ._1_2(controlled_buffer_4_out), ._2_2(controlled_buffer_5_out), ._3_2(controlled_buffer_6_out),
    ._4_2(controlled_buffer_7_out), ._5_2(controlled_buffer_8_out), ._6_2(controlled_buffer_9_out),
    ._7_2(controlled_buffer_10_out), ._8(controlled_buffer_11_out), .Activated(demultiplexer_1_out2),
    ._0(12'hf0), ._1(12'h108), ._2(12'h10), ._3(12'h20), ._4(12'h40), ._5(12'h80), ._6(12'h100), ._7(12'h1f8));
  Constante constante_3 (
    ._1_2(controlled_buffer_4_out), ._2_2(controlled_buffer_5_out), ._3_2(controlled_buffer_6_out),
    ._4_2(controlled_buffer_7_out), ._5_2(controlled_buffer_8_out), ._6_2(controlled_buffer_9_out),
    ._7_2(controlled_buffer_10_out), ._8(controlled_buffer_11_out), .Activated(demultiplexer_1_out3),
    ._0(12'hf0), ._1(12'h108), ._2(12'h8), ._3(12'h8), ._4(12'h70), ._5(12'h8), ._6(12'h108), ._7(12'hf0));
  Constante constante_4 (
    ._1_2(controlled_buffer_4_out), ._2_2(controlled_buffer_5_out), ._3_2(controlled_buffer_6_out),
    ._4_2(controlled_buffer_7_out), ._5_2(controlled_buffer_8_out), ._6_2(controlled_buffer_9_out),
    ._7_2(controlled_buffer_10_out), ._8(controlled_buffer_11_out), .Activated(demultiplexer_1_out7),
    ._0(12'h60), ._1(12'h60), ._2(12'h60), ._3(12'h3fc), ._4(12'h3fc), ._5(12'h60), ._6(12'h60), ._7(12'h60));
  Constante constante_5 (
    ._1_2(controlled_buffer_4_out), ._2_2(controlled_buffer_5_out), ._3_2(controlled_buffer_6_out),
    ._4_2(controlled_buffer_7_out), ._5_2(controlled_buffer_8_out), ._6_2(controlled_buffer_9_out),
    ._7_2(controlled_buffer_10_out), ._8(controlled_buffer_11_out), .Activated(demultiplexer_1_out4),
    ._0(12'h300), ._1(12'h300), ._2(12'h300), ._3(12'h360), ._4(12'h360), ._5(12'h3f8), ._6(12'h60),
    ._7(12'h60));
  Constante constante_6 (
    ._1_2(controlled_buffer_4_out), ._2_2(controlled_buffer_5_out), ._3_2(controlled_buffer_6_out),
    ._4_2(controlled_buffer_7_out), ._5_2(controlled_buffer_8_out), ._6_2(controlled_buffer_9_out),
    ._7_2(controlled_buffer_10_out), ._8(controlled_buffer_11_out), .Activated(demultiplexer_1_out0),
    ._0(12'hf0), ._1(12'h108), ._2(12'h108), ._3(12'h108), ._4(12'h108), ._5(12'h108), ._6(12'h108),
    ._7(12'hf0));
  Constante constante_7 (
    ._1_2(controlled_buffer_4_out), ._2_2(controlled_buffer_5_out), ._3_2(controlled_buffer_6_out),
    ._4_2(controlled_buffer_7_out), ._5_2(controlled_buffer_8_out), ._6_2(controlled_buffer_9_out),
    ._7_2(controlled_buffer_10_out), ._8(controlled_buffer_11_out), .Activated(demultiplexer_1_out6),
    ._0({12{1'b0}}), ._1(12'h3fc), ._2(12'h3fc), ._3({12{1'b0}}), ._4({12{1'b0}}), ._5(12'h3fc),
    ._6(12'h3fc), ._7({12{1'b0}}));
  Constante constante_8 (
    ._1_2(controlled_buffer_4_out), ._2_2(controlled_buffer_5_out), ._3_2(controlled_buffer_6_out),
    ._4_2(controlled_buffer_7_out), ._5_2(controlled_buffer_8_out), ._6_2(controlled_buffer_9_out),
    ._7_2(controlled_buffer_10_out), ._8(controlled_buffer_11_out), .Activated(demultiplexer_1_out5),
    ._0({12{1'b0}}), ._1({12{1'b0}}), ._2({12{1'b0}}), ._3(12'h3fc), ._4(12'h3fc), ._5({12{1'b0}}),
    ._6({12{1'b0}}), ._7({12{1'b0}}));

  // Notes on the sheet:
  //   1
  //   2
  //   3
  //   +
  //   4
  //   0
  //   =
  //   -
endmodule

module caca (
  input  a,
  input  b,
  output c
);

  and and_1 (c, ~a, ~b);  // AND_Gate
endmodule

module aa (
  input  in_1,
  input  in_2,
  output out_3
);

  and and_1 (out_3, ~in_1, ~in_2);  // AND_Gate
endmodule

module Constante (
  input  [11:0] _0,
  input  [11:0] _1,
  input  [11:0] _2,
  input  [11:0] _3,
  input  [11:0] _4,
  input  [11:0] _5,
  input  [11:0] _6,
  input  [11:0] _7,
  input  Activated,
  output [11:0] _1_2,
  output [11:0] _2_2,
  output [11:0] _3_2,
  output [11:0] _4_2,
  output [11:0] _5_2,
  output [11:0] _6_2,
  output [11:0] _7_2,
  output [11:0] _8
);

  assign _1_2 = Activated ? _0 : 12'bz;  // Controlled_Buffer controlled_buffer_1
  assign _2_2 = Activated ? _1 : 12'bz;  // Controlled_Buffer controlled_buffer_2
  assign _3_2 = Activated ? _2 : 12'bz;  // Controlled_Buffer controlled_buffer_3
  assign _4_2 = Activated ? _3 : 12'bz;  // Controlled_Buffer controlled_buffer_4
  assign _5_2 = Activated ? _4 : 12'bz;  // Controlled_Buffer controlled_buffer_5
  assign _6_2 = Activated ? _5 : 12'bz;  // Controlled_Buffer controlled_buffer_6
  assign _7_2 = Activated ? _6 : 12'bz;  // Controlled_Buffer controlled_buffer_7
  assign _8 = Activated ? _7 : 12'bz;  // Controlled_Buffer controlled_buffer_8
endmodule
