// Logisim project Generate Predeterminated.circ as structural Verilog: 1 circuit, main circuit main
module main (
  input  [11:0] in_1,
  input  [11:0] in_2,
  input  [11:0] in_3,
  input  [11:0] in_4,
  input  [11:0] in_5,
  input  [11:0] in_6,
  input  [11:0] in_7,
  input  [11:0] in_8
);

  wire clock_1_out;

  DotMatrix #(.inputtype("row"), .matrixcols(12), .matrixrows(8)) dotmatrix_1 (
    .row0(in_1), .row1(in_2), .row2(in_3), .row3(in_4), .row4(in_5), .row5(in_6), .row6(in_7), .row7(in_8));
  ROM #(.addrWidth(16), .dataWidth(20)) rom_1 ();  // open: addr, data, sel
  Register #(.width(12)) register_1 (.D(in_1), .clk(clock_1_out));  // open: en, Q, clr
  Register #(.width(12)) register_2 (.D(in_2), .clk(clock_1_out));  // open: en, Q, clr
  Register #(.width(12)) register_3 (.D(in_4), .clk(clock_1_out));  // open: en, Q, clr
  Register #(.width(12)) register_4 (.D(in_3), .clk(clock_1_out));  // open: en, Q, clr
  Register #(.width(12)) register_5 (.D(in_5), .clk(clock_1_out));  // open: en, Q, clr
  Clock clock_1 (.out(clock_1_out));
  Register #(.width(12)) register_6 (.D(in_6), .clk(clock_1_out));  // open: en, Q, clr
  Register #(.width(12)) register_7 (.D(in_7), .clk(clock_1_out));  // open: en, Q, clr
  Register #(.width(12)) register_8 (.D(in_8), .clk(clock_1_out));  // open: en, Q, clr

  // Notes on the sheet:
  //   contents of rom_1 (hex, n*v repeats v):
  //   9a804 9aa06 9b008 30000 d0000 30000 d4000 30000 d8000 30000 37*0 c0000
endmodule
